# Fritzing sketch wiring_diagram (saved by Fritzing 0.9.3b)
breadboards: 1

parts:
  U1 = ESP32S-HiLetgo [part_number=ESP32S-HiLetgo]
  Bauteil1 = RFID-RC522-v3
  LCD1 = LCD screen
  LCM1602_IIC1 = LCM1602 IIC [part_number="LCM1602 IIC" chip_label="LCM1602 IIC" package="DIP (Dual Inline) [THT]"]
  J1 = Power Jack [package=power_jack_slot]
  U6 = SWITCH-SPST-2 [package=r_sw_th]
  J2 = Basic Servo
  Bauteil2 = Adafruit VL53L0X Time of Flight Distance Sensor [part_number="Adafruit #3317"]  # not connected
  S1 = Momentary Switch [package=ksa_sealed_tac_switch]
  ZS-042_RTC2 = ZS-042 RTC Module  # not connected

nets:
  N1: U1.GPIO25, LCM1602_IIC1.SDA
  N2: U1.GPIO26, LCM1602_IIC1.SCL
  N3: U1.GPIO12, J2.pulse
  N4: U1.GPIO13, S1.4
  GND: U1.GPIO11, LCM1602_IIC1.GND, J1.GND, J2.gnd
  VCC: U1.VIN, LCM1602_IIC1.VCC, U6.O, J2.vcc
  N5: U1.GPIO6, Bauteil1.3.3V
  N6: U1.GPIO7, Bauteil1.GND
  N7: U1.GPIO19, Bauteil1.SDA
  N8: U1.GND, Bauteil1.SCK, Bauteil1.MOSI
  N9: U1.GPIO21, Bauteil1.MISO
  N10: U1.GPIO23, Bauteil1.RST
  VSS: LCD1.VSS, LCM1602_IIC1.VSS
  VDD: LCD1.VDD, LCM1602_IIC1.VDD
  N11: LCD1.V0, LCM1602_IIC1.V0
  N12: LCD1.RS, LCM1602_IIC1.RS
  N13: LCD1.R/W, LCM1602_IIC1.RW
  N14: LCD1.E, LCM1602_IIC1.E
  N15: LCD1.DB0, LCM1602_IIC1.D0
  N16: LCD1.DB1, LCM1602_IIC1.D1
  N17: LCD1.DB2, LCM1602_IIC1.D2
  N18: LCD1.DB3, LCM1602_IIC1.D3
  N19: LCD1.DB4, LCM1602_IIC1.D4
  N20: LCD1.DB5, LCM1602_IIC1.D5
  N21: LCD1.DB6, LCM1602_IIC1.D6
  N22: LCD1.DB7, LCM1602_IIC1.D7
  N23: LCD1.LED+, LCM1602_IIC1.A
  N24: LCD1.LED-, LCM1602_IIC1.K
  N25: LCM1602_IIC1.LED_A, LCM1602_IIC1.LED_B
  N26: J1.PWR, U6.P

notes:
  SDA - GPIO25 Blue
  SCL - GPIO26
  Green
  Button-PIN 13
  Servo-PIN 12
  5V IN

custom parts:
  ESP32S-HiLetgo: HiLetgo ESP-WROOM-32 ESP32 ESP-32S Development Board 2.4GHz Dual-Mode WiFi + Bluetooth Dual Cores Microcontroller The ESP32 integrated with Antenna switches, RF Balun, power amplifiers, low-noise amplifiers, filters, and management modules, and the entire solution occupies the least area of PCB. 2.4 GHz Wi-Fi plus Bluetooth dual-mode chip, with TSMC Ultra-low power consumption 40nm technology,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
  RFID-RC522-v3: A simple China made RFID-RC522 Reader (6x4 cm); do check the pin labels, as this is a MFRC522 based clone.
  LCM1602 IIC: I2C-Module to use a 1602 or 2004 LCD on with the wire.h libory Serial LCD Modul
  Adafruit VL53L0X Time of Flight Distance Sensor: The VL53L0X is a Time of Flight distance sensor like no other you've used! The sensor contains a very tiny invisible laser source, and a matching sensor. The VL53L0X can detect the "time of flight", or how long the light has taken to bounce back to the sensor. Since it uses a very narrow light source, it is good for determining distance of only the surface directly in front of it. Unlike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
